# Fritzing sketch CIRCUITO_1 (saved by Fritzing 0.9.3b)

parts:
  R1 = Resistor [tolerance=±5% resistance=330 package=THT]
  TTP223B1 = TTP223B Capacitive Touch Sensor Module
  S1 = H-Bridge with L298N
  Componente1 = Arduino Nano (Rev3.0)
  hc-sr1 = hc-sr04
  hc-sr2 = hc-sr04
  hc-sr3 = hc-sr04
  M1 = DC Motor
  JACK1 = 2.1mm Barrel Jack with Terminal Block
  JACK2 = 2.1mm Barrel Jack with Terminal Block
  Bat1 = battery_holder_single_18650
  Bat2 = battery_holder_single_18650
  Bat3 = battery_holder_single_18650
  Bat4 = battery_holder_single_18650
  A1 = battery capcity indicator module 1s-8s [package=THT]
  GY1 = MPU-6050 Board GY-521 [form="♀ (female)" package=THT]
  J1 = Basic Servo
  CONN1 = USB connector [package=THT]
  A2 = HuskyLens-Vision-Sensor_1
  U1 = SWITCH_SPDT [package=kps-1290]
  CONN2 = USB connector [package=THT]

nets:
  GND: R1.Pin_0, TTP223B1.GND, S1.GND, Componente1.GND, hc-sr1.GND, hc-sr2.GND, hc-sr3.GND, JACK2.NEG, GY1.pin2, J1.gnd, CONN1.d-, A2.pin3, CONN2.GND, CONN2.chassis6
  N1: R1.Pin_1, TTP223B1.SIG, Componente1.D12/MISO
  VCC: TTP223B1.VCC, S1.5V, Componente1.5V, hc-sr1.VCC, hc-sr2.VCC, hc-sr3.VCC, GY1.pin1, A2.pin4, U1.S
  N2: S1.12V, JACK2.POS
  N3: S1.IN3, Componente1.D5
  N4: S1.IN4, Componente1.D4
  N5: S1.ENB, Componente1.D3
  N6: S1.M1-02, S1.M2-01, S1.M2-02, M1.pin_1, M1.pin_2
  N7: Componente1.D6, hc-sr3.Echo
  N8: Componente1.D7, hc-sr3.Trig
  N9: Componente1.D8, hc-sr2.Trig
  N10: Componente1.D9, hc-sr2.Echo
  N11: Componente1.D10, hc-sr1.Echo
  N12: Componente1.D11/MOSI, hc-sr1.Trig
  N13: Componente1.A5, GY1.pin3, A2.pin2
  N14: Componente1.A4, GY1.pin4, A2.pin1
  N15: Componente1.D13/SCK, J1.pulse
  N16: JACK1.POS, Bat3.+#1, A1.pin1
  N17: JACK1.NEG, Bat4.+#0, A1.pin2
  N18: Bat1.+#0, Bat4.+#1
  N19: Bat1.+#1, Bat2.+#0
  N20: Bat2.+#1, Bat3.+#0
  VCC_2: J1.vcc, CONN2.5V
  N21: CONN1.d+, U1.P

custom parts:
  TTP223B Capacitive Touch Sensor Module: The TTP223B capacitive touch sensor module uses the TTP223B IC. The appropriate voltage is approximately 2 to 5.5 volts.
  H-Bridge with L298N: h-bridge
  battery_holder_single_18650: single 18650 battery holder
  battery capcity indicator module 1s-8s: battery capcity indicator module 1s-8s.
  MPU-6050 Board GY-521: Acelerometro y Giroscopio MPU-6050 Board GY-521
  HuskyLens-Vision-Sensor_1: Huskylens is an easy-to-use AI Camera | Vision Sensor. DFrobot Huskylens is equipped with multiple functions, such as face recognition, object tracking, object recognition, line tracking, color recognition, and tag(QR code) recognition.
